# Fritzing sketch mini robot (saved by Fritzing 0.9.5d)
stripboards: 3

parts:
  ESP32 = ESP32 DevKitc V4
  DFPlayer = DFRobot DFPlayer Mini [part_number=DFR0299]
  MIC = ADMP421 [package=admp421]
  N20_Motor1 = N20 Motor
  motor_driver_-_DRV8833 = DollaTek DRV8833
  N20_Motor2 = N20 Motor
  range_sensor_-_GY-530_VL53LOX = GY-VL53L0XV2 Laser Ranger Module
  gyroscope = InvenSense MPU6050
  3_LIPO_BATTERIES_(~12V) = Battery block 9V
  S1 = Toggle Switch [package=THT]
  power_indicator = LED - 5mm [color="Blue (430nm)" package="5 mm [THT]"]
  LDR = Photocell (LDR) [package=THT]
  U1 = WS2812 RGB LED matrix 8x8
  IR_sensor = TCRT5000 sensor module [part_number=151608]  # not connected
  R1 = Resistor [tolerance=±5% resistance=330 package="1206 [SMD]"]
  3S_4A_charger = TP4056 [chip_label=TP4056 package="DIP (Dual Inline) [THT]"]
  J1 = Piezo Speaker
  OLED = Grove OLED 128x96
  IR_sensor1 = TCRT5000 sensor module [part_number=151608]  # not connected
  R2 = Resistor [tolerance=±5% resistance=10k package="1206 [SMD]"]
  BAT1 = Battery Holders [package=battery-aaa]  # not connected
  BAT2 = Battery Holders [package=battery-aa-panel]  # not connected
  JP1 = Header 2 [package=screwterminal-3.5mm-2_lock]  # not connected
  M1 = RioRand LM2596  # not connected
  lm2596_buck = LM2596 step down module
  A1 = battery capcity indicator module 1s-8s [package=THT]

nets:
  N1: ESP32.IO16, N20_Motor1.pin_1, motor_driver_-_DRV8833.pin_1, motor_driver_-_DRV8833.pin_7, motor_driver_-_DRV8833.pin_12
  N2: ESP32.IO17, N20_Motor1.pin_6, motor_driver_-_DRV8833.pin_2
  N3: ESP32.IO18, motor_driver_-_DRV8833.pin_5, N20_Motor2.pin_6
  N4: ESP32.IO19, motor_driver_-_DRV8833.pin_6
  N5: ESP32.IO21, range_sensor_-_GY-530_VL53LOX.SDA, gyroscope.SDA, OLED.SDA
  N6: ESP32.RX, DFPlayer.TX
  N7: ESP32.TX, DFPlayer.RX
  N8: ESP32.IO22, range_sensor_-_GY-530_VL53LOX.SCL, gyroscope.SCL, OLED.SCL
  N9: ESP32.GND#18, lm2596_buck.OUT+
  3V3: ESP32.3V3, MIC.VDD, LDR.pin_1, OLED.VCC
  N10: ESP32.VN, motor_driver_-_DRV8833.pin_9, motor_driver_-_DRV8833.pin_10, N20_Motor2.pin_1, 3_LIPO_BATTERIES_(~12V).-, S1.L2, power_indicator.anode, R1.Pin_0, 3S_4A_charger.pin5, lm2596_buck.IN+, lm2596_buck.IN-, lm2596_buck.OUT-
  GND: ESP32.GND#32, DFPlayer.GND-1, DFPlayer.GND-2, MIC.GND, range_sensor_-_GY-530_VL53LOX.GND, gyroscope.GND, LDR.pin_0, U1.GND, J1.pin1, OLED.GND, R2.Pin_0, R2.Pin_1
  VCC: DFPlayer.VCC, range_sensor_-_GY-530_VL53LOX.VCC, gyroscope.VCC, U1.VCC
  N11: DFPlayer.SPK_1, J1.pin2
  N12: 3_LIPO_BATTERIES_(~12V).+, S1.COM
  N13: S1.L1, 3S_4A_charger.pin4
  N14: 3S_4A_charger.pin3, A1.pin1
  N15: 3S_4A_charger.pin6, A1.pin2

custom parts:
  ESP32 DevKitc V4: ESP32-DevKitC board with ESP32-WROOM-32 module. ESP32-DevKitC V4 is a small-sized ESP32-based development board produced by Espressif. Most of the pins on the ESP module are broken out to the pin headers on the board. The pins D0, D1, D2, D3, CMD and CLK are used internally for communication between ESP32 and SPI flash memory. They are grouped on both sides near the USB connector. Avoid using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
  DollaTek DRV8833: DollaTek DRV8833 1.5A 2-Channel DC Motor Drive Board
  GY-VL53L0XV2 Laser Ranger Module: The GY-VL53L0XV2 is based on the VL53L0X from ST Microelectronics, a time-of-flight ranging system integrated into a compact module.
  WS2812 RGB LED matrix 8x8: WS2812 matrix 8x8
  TCRT5000 sensor module: breakout board with TCRT5000
  TP4056: A DIP stand-in part for whatever IC you want. With 6 pins on a 300mil dual inline package (DIP) footprint.
  LM2596 step down module: LM2596 DC-DC step down power supply module 3 A.
  battery capcity indicator module 1s-8s: battery capcity indicator module 1s-8s.
